// Digital circuit ktst.dig as structural Verilog
module ktst (
  input  clk,
  output [2:0] delay,
  output strobe,
  output enable,
  output clock,
  output en2,
  output strobeOut
);

  wire keyboard_av, widenstrobe_ovf;
  wire [3:0] lastKey_q;
  wire [6:0] key_d;
  wire [7:4] lastKey_q_2;
  wire [15:7] keyboard_d;

  and and_1 (enable, keyboard_av, ~strobe);  // And
  Register #(.Bits(8)) lastKey (.D({1'b0, key_d}), .C(clk), .en(enable), .Q({lastKey_q_2, lastKey_q}));
  Keyboard keyboard (.C(clk), .en(enable), .D({keyboard_d, key_d}), .av(keyboard_av));
  Counter #(.Bits(3)) widenstrobe (.en(strobe), .C(clk), .clr(1'b0), .out(delay), .ovf(widenstrobe_ovf));
  Seven_Seg_Hex seven_seg_hex_1 (.d(lastKey_q_2), .dp(1'b1));
  Register register_1 (.D(enable), .C(clk), .en(en2), .Q(strobe));
  or or_1 (en2, enable, widenstrobe_ovf);
  D_FF d_ff_1 (.D(strobe), .C(clk), .Q(strobeOut));  // open: nQ
  Seven_Seg_Hex seven_seg_hex_2 (.d(lastKey_q), .dp(strobeOut));

  assign clock = clk;
endmodule
